# Fritzing sketch IRglove (saved by Fritzing 0.9.3b)
breadboards: 1

parts:
  Part1 = Arduino Uno (Rev3)
  IR1 = TSOP312.., 314.. [package=THT]
  Q1 = TRANSISTOR_NPN [package=to-92-ammo]
  LED1 = LED - 3mm [color="Infrared (940nm)" package="3 mm [THT]"]
  J1 = female pin header, 2 pins [form="♀ (female)"]
  J2 = female pin header, 2 pins [form="♀ (female)"]
  J3 = female pin header, 2 pins [form="♀ (female)"]
  R1 = Resistor [tolerance=±5% resistance=330 package="1206 [SMD]"]
  R2 = Resistor [tolerance=±5% resistance=10 package="1206 [SMD]"]

nets:
  N1: Part1.D8, J2.pin2
  N2: Part1.D9_PWM, J1.pin2
  N3: Part1.D12/MISO, IR1.GND
  N4: Part1.D3_PWM, R1.Pin_1
  N5: Part1.5V, IR1.Data, LED1.anode
  N6: Part1.GND, IR1.Vs, Q1.C, J3.pin2
  N7: Q1.E, R2.Pin_1
  N8: Q1.B, R1.Pin_0
  N9: LED1.cathode, R2.Pin_0
